# Fritzing sketch thermistor (saved by Fritzing 1.0.5)
breadboards: 1

parts:
  R1 = Resistor [tolerance=±5% power=0.25W resistance=10k package=THT]
  Mod1 = Raspberry Pi Pico W
  R2 = Temperature Sensor (Thermistor) [thermistor_type=NTC package=THT]
  OLED1 = OLED 128x64 I2C Monochrome Display GND-VDD

nets:
  N1: R1.Pin_0, Mod1.pin_36, OLED1.VDD
  N2: R1.Pin_1, Mod1.pin_31, R2.pin_1
  N3: Mod1.pin_1, OLED1.SDA
  N4: Mod1.pin_2, OLED1.SCK
  N5: Mod1.pin_3, Mod1.pin_8, Mod1.pin_13, Mod1.pin_18, Mod1.pin_23, Mod1.pin_28, Mod1.pin_33, Mod1.pin_38, R2.pin_0, OLED1.GND

custom parts:
  Raspberry Pi Pico W: Raspberry Pi Pico W. Based around the RP2040 microcontroller the Pico W is a low cost microcontroller device bringing Raspberry Pi quality, cost, and easy of use to the microcontroller space. The areas marked KEEPOUT in pcb silkscreen should not have traces running through them to avoid shorts on a soldered in module!
  OLED 128x64 I2C Monochrome Display GND-VDD: OLED 128x64 I2C Monochrome Display. Note: there are two variants of this part, this one is the GND VDD SCK SDA variant. The other is VDD GND SCK SDA. Make sure you select the part that matches your module as using the incorrect part will probably destroy your module! In addition the mounting holes are marked on silkscreen but not by default drilled. If you want drilled mounting holes, copy a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
